// Logisim project CPU Control Hazard.circ as structural Verilog: 10 circuits, main circuit Single cycle CPU
module instrction_memory (
  input  [11:0] in_1,
  output [15:0] out_2
);

  ROM #(.addrWidth(12), .dataWidth(16)) rom_1 (.addr(in_1), .data(out_2));  // open: sel

  // Notes on the sheet:
  //   Instruction_Memory
  //   contents of rom_1 (hex, n*v repeats v):
  //   a384 0 8354 0 373 0 2040 0 2081 0 20c2 0 890a 0 1921 0 1520 0 14f2 0 4182 0 1290 0 403b 0 3100 0
  //   4003 0 55c 0 1b68 0 403f 0 4e9 0 2040 0 2285 0 22c6 0 4e0 0 3100 0 4036
endmodule

module data_memory (
  input  [15:0] in_1,
  input  [15:0] in_2,
  input  in_3,
  input  in_4,
  input  in_5,
  output [15:0] out_6
);

  RAM #(.addrWidth(12), .dataWidth(16), .bus("separate")) ram_1 (
    .addr(in_1[11:0]), .din(in_2), .data(out_6), .str(in_3), .clk(in_5), .ld(in_4));  // open: sel, clr

  // Notes on the sheet:
  //   Data_Memory
endmodule

module jj (
  input  [5:0] in_1
);
endmodule

module ControlSrc (
  input  z,
  input  x,
  input  c,
  input  v,
  input  g,
  output JALR,
  output JumpCtrl,
  output H,
  output S,
  output RegWrite,
  output M,
  output N,
  output ALUSrc,
  output MemoryWrite,
  output MemoryRead,
  output MemoryReg
);

  wire and_1_out, and_2_out, and_3_out, and_4_out, and_5_out, and_6_out, and_7_out, and_8_out, and_9_out,
       and_10_out, and_11_out, and_12_out, and_13_out, and_14_out, and_15_out, and_16_out, and_17_out,
       and_18_out, and_19_out, and_20_out, and_21_out, and_22_out, and_23_out, and_24_out, and_26_out,
       and_27_out, and_28_out, and_29_out, and_31_out, and_32_out, not_1_out, not_2_out, not_3_out,
       not_4_out, not_5_out, not_6_out, not_7_out, not_8_out, not_9_out, not_10_out, not_11_out, not_12_out,
       not_13_out, not_14_out, not_15_out, not_16_out, not_18_out, not_19_out, not_20_out, not_21_out,
       or_1_out, or_5_out, or_6_out, or_7_out;

  not not_1 (not_1_out, z);
  not not_2 (not_2_out, z);
  not not_3 (not_3_out, c);
  not not_4 (not_4_out, c);
  not not_5 (not_5_out, c);
  not not_6 (not_6_out, g);
  not not_7 (not_7_out, z);
  not not_8 (not_8_out, v);
  not not_9 (not_9_out, c);
  not not_10 (not_10_out, g);
  not not_11 (not_11_out, x);
  not not_12 (not_12_out, c);
  not not_13 (not_13_out, g);
  not not_14 (not_14_out, c);
  not not_15 (not_15_out, x);
  not not_16 (not_16_out, c);
  not not_17 (MemoryRead, g);
  not not_18 (not_18_out, x);
  and and_1 (and_1_out, not_1_out, c);
  and and_2 (and_2_out, c, v);
  and and_3 (and_3_out, not_2_out, x);
  and and_4 (and_4_out, c, v);
  and and_5 (and_5_out, z, x);
  and and_6 (and_6_out, not_3_out, g);
  and and_7 (and_7_out, z, x);
  and and_8 (and_8_out, not_4_out, v);
  and and_9 (and_9_out, x, not_5_out);
  and and_10 (and_10_out, v, not_6_out);
  and and_11 (and_11_out, not_7_out, not_8_out);
  and and_12 (and_12_out, not_9_out, not_10_out);
  not not_19 (not_19_out, z);
  and and_13 (and_13_out, not_11_out, c);
  and and_14 (and_14_out, x, not_12_out);
  and and_15 (and_15_out, z, x);
  and and_16 (and_16_out, v, not_13_out);
  and and_17 (and_17_out, x, c);
  and and_18 (and_18_out, z, not_14_out);
  and and_19 (and_19_out, z, not_15_out);
  and and_20 (and_20_out, not_16_out, g);
  and and_21 (and_21_out, z, not_18_out);
  not not_20 (not_20_out, c);
  or or_1 (or_1_out, and_1_out, and_2_out);
  or or_2 (JALR, or_1_out, and_22_out);
  and and_22 (and_22_out, x, c);
  and and_23 (and_23_out, and_3_out, and_4_out);
  or or_3 (JumpCtrl, and_23_out, and_24_out);
  and and_24 (and_24_out, and_5_out, and_6_out);
  and and_25 (H, and_7_out, and_8_out);
  not not_21 (not_21_out, z);
  or or_4 (S, not_21_out, and_26_out);
  and and_26 (and_26_out, and_9_out, and_10_out);
  or or_5 (or_5_out, and_11_out, and_12_out);
  or or_6 (or_6_out, or_5_out, and_27_out);
  and and_27 (and_27_out, not_19_out, g);
  and and_28 (and_28_out, and_13_out, v);
  or or_7 (or_7_out, and_28_out, and_29_out);
  and and_29 (and_29_out, and_14_out, v);
  and and_30 (M, and_15_out, and_16_out);
  and and_31 (and_31_out, and_17_out, v);
  or or_8 (N, and_31_out, and_32_out);
  and and_32 (and_32_out, and_18_out, g);
  and and_33 (MemoryWrite, and_19_out, and_20_out);
  and and_34 (MemoryReg, and_21_out, not_20_out);
  or or_9 (RegWrite, or_6_out, or_7_out);

  assign ALUSrc = z;
endmodule

module ALUConrol (
  input  z,
  input  x,
  input  c,
  input  v,
  input  g,
  output A,
  output B,
  output C_2,
  output D
);

  wire and_1_out, and_4_out, and_5_out, and_6_out, and_7_out, and_8_out, and_9_out, and_10_out, and_11_out,
       and_12_out, not_1_out, not_2_out, not_3_out, not_4_out, not_5_out, not_6_out, not_7_out, not_8_out,
       not_9_out, not_10_out, or_1_out;

  not not_1 (not_1_out, x);
  not not_2 (not_2_out, z);
  not not_3 (not_3_out, z);
  not not_4 (not_4_out, x);
  not not_5 (not_5_out, z);
  and and_1 (and_1_out, z, not_1_out);
  not not_6 (not_6_out, c);
  not not_7 (not_7_out, c);
  not not_8 (not_8_out, v);
  not not_9 (not_9_out, g);
  and and_2 (B, not_2_out, c);
  and and_3 (C_2, not_3_out, v);
  not not_10 (not_10_out, z);
  and and_4 (and_4_out, not_4_out, c);
  and and_5 (and_5_out, v, g);
  and and_6 (and_6_out, not_5_out, x);
  or or_1 (or_1_out, and_6_out, and_7_out);
  and and_7 (and_7_out, and_1_out, not_6_out);
  and and_8 (and_8_out, z, not_7_out);
  and and_9 (and_9_out, and_8_out, and_10_out);
  and and_10 (and_10_out, not_8_out, not_9_out);
  and and_11 (and_11_out, not_10_out, g);
  or or_2 (D, and_11_out, and_12_out);
  and and_12 (and_12_out, and_4_out, and_5_out);
  or or_3 (A, or_1_out, and_9_out);
endmodule

module BranchSelect (
  input  z,
  input  x,
  input  c,
  input  v,
  input  g,
  output Q,
  output W,
  output E
);

  wire and_1_out, and_2_out, and_3_out, and_4_out, and_5_out, and_6_out, and_7_out, and_8_out, and_9_out,
       and_10_out, and_11_out, and_12_out, and_14_out, and_15_out, and_16_out, and_17_out, and_18_out,
       not_1_out, not_2_out, not_3_out, not_4_out, not_5_out, not_6_out, not_7_out, or_2_out;

  not not_1 (not_1_out, g);
  not not_2 (not_2_out, v);
  not not_3 (not_3_out, x);
  not not_4 (not_4_out, v);
  not not_5 (not_5_out, g);
  not not_6 (not_6_out, v);
  and and_1 (and_1_out, z, x);
  and and_2 (and_2_out, c, not_1_out);
  and and_3 (and_3_out, z, x);
  and and_4 (and_4_out, c, v);
  and and_5 (and_5_out, z, c);
  and and_6 (and_6_out, not_2_out, g);
  and and_7 (and_7_out, z, not_3_out);
  and and_8 (and_8_out, not_4_out, not_5_out);
  and and_9 (and_9_out, z, x);
  and and_10 (and_10_out, c, not_6_out);
  not not_7 (not_7_out, g);
  and and_11 (and_11_out, and_1_out, and_2_out);
  or or_1 (Q, and_11_out, and_12_out);
  and and_12 (and_12_out, and_3_out, and_4_out);
  and and_13 (W, and_5_out, and_6_out);
  and and_14 (and_14_out, and_7_out, and_8_out);
  or or_2 (or_2_out, and_14_out, and_15_out);
  and and_15 (and_15_out, and_9_out, and_10_out);
  and and_16 (and_16_out, z, x);
  and and_17 (and_17_out, and_16_out, and_18_out);
  and and_18 (and_18_out, c, not_7_out);
  or or_3 (E, or_2_out, and_17_out);
endmodule

module BranchSelect1 (
  input  z,
  input  x,
  input  c,
  input  v,
  input  g,
  output Q,
  output W,
  output E
);

  wire and_1_out, and_2_out, and_3_out, and_4_out, and_5_out, and_6_out, and_7_out, not_1_out, not_2_out,
       not_3_out, not_4_out, not_5_out, not_6_out, not_7_out, not_8_out, not_9_out;

  not not_1 (not_1_out, g);
  not not_2 (not_2_out, x);
  not not_3 (not_3_out, v);
  not not_4 (not_4_out, v);
  not not_5 (not_5_out, x);
  not not_6 (not_6_out, v);
  not not_7 (not_7_out, g);
  not not_8 (not_8_out, v);
  not not_9 (not_9_out, g);
  and and_1 (and_1_out, z, x, c, not_1_out);
  and and_2 (and_2_out, z, x, c, v);
  and and_3 (and_3_out, z, not_2_out, not_3_out, g);
  and and_4 (and_4_out, z, x, c, not_4_out);
  and and_5 (and_5_out, z, not_5_out, not_6_out, not_7_out);
  and and_6 (and_6_out, z, x, c, not_8_out, g);
  and and_7 (and_7_out, z, x, c, v, not_9_out);
  or or_1 (Q, and_1_out, and_2_out);
  or or_2 (W, and_3_out, and_4_out);
  or or_3 (E, and_5_out, and_6_out, and_7_out);
endmodule

module Pipline_CPU (
);

  wire ALUSrc, Clock, JALR, JumpCtrl, MemoryRead, MemoryReg, MemoryWrite, RegWrite;
  wire [1:0] JAL, RegDst;
  wire [2:0] BrancheSelect, multiplexer_2_out;
  wire [3:0] ALU_CONT, Opcode;
  wire [11:0] DataLUI, multiplexer_1_out, Next_PC, PC;
  wire [15:0] ALU_Res, bit_extender_1_out, bit_extender_2_out, bit_extender_3_out, dataWrite, LUI_Res,
       multiplexer_3_out, multiplexer_4_out, RA, ram_1_data, RB;

  Clock clock_1 (.out(Clock));
  Multiplexer #(.width(12), .enable("false")) multiplexer_1 (
    .in0(DataLUI), .in1(RA[11:0]), .out(multiplexer_1_out), .sel(JALR));
  assign bit_extender_1_out = {{4{1'b0}}, DataLUI};  // Bit_Extender bit_extender_1
  pc_main main_1 (
    .jump_or_branch_value(multiplexer_1_out), .in_4(RA), .in_6(RB), .pc(PC), .jump(JumpCtrl),
    .in_7(BrancheSelect), .in_5(Clock), .out_8(Next_PC));  // open: out_10, in_3
  Shifter #(.width(16)) shifter_1 (.in(bit_extender_1_out), .\dist (4'b0100), .out(LUI_Res));
  ll ll_1 (
    .Function(DataLUI[2:0]), .OPcode(Opcode), .out_5(JALR), .out_7(JumpCtrl), .out_9(RegDst[1]),
    .out_10(RegDst[0]), .out_11(RegWrite), .out_12(JAL[1]), .out_13(JAL[0]), .out_14(ALUSrc),
    .out_15(MemoryWrite), .out_16(MemoryRead), .out_17(MemoryReg), .out_18(BrancheSelect[2]),
    .out_19(BrancheSelect[1]), .out_20(BrancheSelect[0]), .out_3(ALU_CONT[3]), .out_6(ALU_CONT[1]),
    .out_4(ALU_CONT[2]), .out_8(ALU_CONT[0]));
  ROM #(.addrWidth(12), .dataWidth(16)) rom_1 (.addr(PC), .data({Opcode, DataLUI}));  // open: sel
  Multiplexer #(.select(2), .width(3), .enable("false")) multiplexer_2 (
    .in0(DataLUI[8:6]), .in1(DataLUI[5:3]), .in2(3'b111), .in3(3'b001), .out(multiplexer_2_out), .sel(RegDst));
  Reg_File reg_file_1 (
    .register_write(multiplexer_2_out), .reg_write(RegWrite), .write_data(multiplexer_3_out),
    .read_register_1(DataLUI[11:9]), .read_data_1(RA), .read_data_2(RB), .read_register_2(DataLUI[8:6]),
    .clock(Clock));
  assign bit_extender_2_out = {{4{1'b0}}, Next_PC};  // Bit_Extender bit_extender_2
  Multiplexer #(.select(2), .width(16), .enable("false")) multiplexer_3 (
    .in0(dataWrite), .in1(bit_extender_2_out), .in2(LUI_Res), .out(multiplexer_3_out), .sel(JAL));  // open: in3
  assign bit_extender_3_out = {{10{DataLUI[5]}}, DataLUI[5:0]};  // Bit_Extender bit_extender_3
  Multiplexer #(.width(16), .enable("false")) multiplexer_4 (
    .in0(RB), .in1(bit_extender_3_out), .out(multiplexer_4_out), .sel(ALUSrc));
  alu_main main_2 (.A(RA), .B(multiplexer_4_out), .ALU_CONT(ALU_CONT), .out_4(ALU_Res));
  RAM #(.addrWidth(12), .dataWidth(16), .bus("separate")) ram_1 (
    .addr(ALU_Res[11:0]), .din(RB), .data(ram_1_data), .str(MemoryWrite), .clk(Clock), .ld(MemoryRead));  // open: sel, clr
  Multiplexer #(.width(16), .enable("false")) multiplexer_5 (
    .in0(ALU_Res), .in1(ram_1_data), .out(dataWrite), .sel(MemoryReg));

  // Other names for the same wires on the sheet: Funct[2:0] = DataLUI[2:0]; imm6[5:0] = DataLUI[5:0];
  //   imm12[11:0] = DataLUI; Rd[2:0] = DataLUI[5:3]; Rt[2:0] = DataLUI[8:6]; Rs[2:0] = DataLUI[11:9]

  // Notes on the sheet:
  //   Instruction_Memory
  //   contents of rom_1 (hex, n*v repeats v):
  //   a384 0 8354 0 35b 0 2040 0 2081 0 20c2 0 890a 0 1921 0 1520 0 14f2 0 4c02 0 1290 0 403b 0 3100 0
  //   b024 0 55c 0 1b68 0 403f 0 4e9 0 2040 0 2285 0 22c6 0 4e0 0 3100 0 1e06
  //   Data_Memory
endmodule

module Single_cycle_CPU (
  output [15:0] out_1
);

  wire ALUSrc, Clock, JALR, JumpCtrl, MemoryRead, MemoryReg, MemoryWrite, RegWrite;
  wire [1:0] JAL, RegDst;
  wire [2:0] BrancheSelect, multiplexer_2_out;
  wire [3:0] ALU_CONT, Opcode;
  wire [11:0] DataLUI, multiplexer_1_out, Next_PC, PC;
  wire [15:0] ALU_Res, bit_extender_1_out, bit_extender_2_out, bit_extender_3_out, dataWrite, LUI_Res,
       multiplexer_4_out, RA, ram_1_data, RB;

  Multiplexer #(.width(12), .enable("false")) multiplexer_1 (
    .in0(DataLUI), .in1(RA[11:0]), .out(multiplexer_1_out), .sel(JALR));
  assign bit_extender_1_out = {{4{1'b0}}, DataLUI};  // Bit_Extender bit_extender_1
  pc_main main_1 (
    .jump_or_branch_value(multiplexer_1_out), .in_4(RA), .in_6(RB), .pc(PC), .jump(JumpCtrl),
    .in_7(BrancheSelect), .in_5(Clock), .out_8(Next_PC));  // open: out_10, in_3
  Shifter #(.width(16)) shifter_1 (.in(bit_extender_1_out), .\dist (4'b0100), .out(LUI_Res));
  Clock clock_1 (.out(Clock));
  ROM #(.addrWidth(12), .dataWidth(16)) rom_1 (.addr(PC), .data({Opcode, DataLUI}));  // open: sel
  ll ll_1 (
    .Function(DataLUI[2:0]), .OPcode(Opcode), .out_5(JALR), .out_7(JumpCtrl), .out_9(RegDst[1]),
    .out_10(RegDst[0]), .out_11(RegWrite), .out_12(JAL[1]), .out_13(JAL[0]), .out_14(ALUSrc),
    .out_15(MemoryWrite), .out_16(MemoryRead), .out_17(MemoryReg), .out_18(BrancheSelect[2]),
    .out_19(BrancheSelect[1]), .out_20(BrancheSelect[0]), .out_3(ALU_CONT[3]), .out_6(ALU_CONT[1]),
    .out_4(ALU_CONT[2]), .out_8(ALU_CONT[0]));
  Multiplexer #(.select(2), .width(3), .enable("false")) multiplexer_2 (
    .in0(DataLUI[8:6]), .in1(DataLUI[5:3]), .in2(3'b111), .in3(3'b001), .out(multiplexer_2_out), .sel(RegDst));
  Reg_File reg_file_1 (
    .register_write(multiplexer_2_out), .reg_write(RegWrite), .write_data(out_1),
    .read_register_1(DataLUI[11:9]), .read_data_1(RA), .read_data_2(RB), .read_register_2(DataLUI[8:6]),
    .clock(Clock));
  assign bit_extender_2_out = {{4{1'b0}}, Next_PC};  // Bit_Extender bit_extender_2
  Multiplexer #(.select(2), .width(16), .enable("false")) multiplexer_3 (
    .in0(dataWrite), .in1(bit_extender_2_out), .in2(LUI_Res), .out(out_1), .sel(JAL));  // open: in3
  assign bit_extender_3_out = {{10{DataLUI[5]}}, DataLUI[5:0]};  // Bit_Extender bit_extender_3
  Multiplexer #(.width(16), .enable("false")) multiplexer_4 (
    .in0(RB), .in1(bit_extender_3_out), .out(multiplexer_4_out), .sel(ALUSrc));
  alu_main main_2 (.A(RA), .B(multiplexer_4_out), .ALU_CONT(ALU_CONT), .out_4(ALU_Res));
  RAM #(.addrWidth(12), .dataWidth(16), .bus("separate")) ram_1 (
    .addr(ALU_Res[11:0]), .din(RB), .data(ram_1_data), .str(MemoryWrite), .clk(Clock), .ld(MemoryRead));  // open: sel, clr
  Multiplexer #(.width(16), .enable("false")) multiplexer_5 (
    .in0(ALU_Res), .in1(ram_1_data), .out(dataWrite), .sel(MemoryReg));

  // Other names for the same wires on the sheet: Funct[2:0] = DataLUI[2:0]; imm6[5:0] = DataLUI[5:0];
  //   imm12[11:0] = DataLUI; Rd[2:0] = DataLUI[5:3]; Rt[2:0] = DataLUI[8:6]; Rs[2:0] = DataLUI[11:9]

  // Notes on the sheet:
  //   Instruction_Memory
  //   contents of rom_1 (hex, n*v repeats v):
  //   a384 0 8354 0 35b 0 2040 0 2081 0 20c2 0 890a 0 1921 0 1520 0 14f2 0 4c02 0 1290 0 403b 0 3100 0
  //   b024 0 55c 0 1b68 0 403f 0 4e9 0 2040 0 2285 0 22c6 0 4e0 0 3100 0 1e06
  //   Data_Memory
endmodule

module Control_Hazard (
  input  [2:0] Rd_ALU,
  input  RW_ALU,
  input  [2:0] Rd_MEM,
  input  RW_MEM,
  input  RW_WB,
  input  [2:0] Rd_WB,
  input  [2:0] Rs,
  input  [2:0] Rt,
  input  Memomry_Read,
  output [1:0] forward_A,
  output [1:0] forward_B,
  output stall
);

  wire comparator_1_gt, comparator_2_lt, comparator_3_gt, comparator_4_lt, comparator_5_gt, comparator_6_lt,
       or_4_out, Rd1, Rd2, Rd3, Rs1, Rs2, Rs3, Rt1, Rt2, Rt3;
  wire [2:0] selector1, selector2;

  Comparator #(.width(3)) comparator_1 (.a(Rd_ALU), .b(3'b000), .gt(comparator_1_gt));  // open: eq, lt
  Comparator #(.width(3)) comparator_2 (.a(Rd_ALU), .b(3'b000), .lt(comparator_2_lt));  // open: gt, eq
  Comparator #(.width(3)) comparator_3 (.a(Rd_MEM), .b(3'b000), .gt(comparator_3_gt));  // open: eq, lt
  Comparator #(.width(3)) comparator_4 (.a(Rd_MEM), .b(3'b000), .lt(comparator_4_lt));  // open: gt, eq
  Comparator #(.width(3)) comparator_5 (.a(Rd_WB), .b(3'b000), .gt(comparator_5_gt));  // open: eq, lt
  Comparator #(.width(3)) comparator_6 (.a(Rd_WB), .b(3'b000), .lt(comparator_6_lt));  // open: gt, eq
  Comparator #(.width(3)) comparator_7 (.a(Rs), .b(Rd_ALU), .eq(Rs1));  // open: gt, lt
  Comparator #(.width(3)) comparator_8 (.a(Rs), .b(Rd_MEM), .eq(Rs2));  // open: gt, lt
  Comparator #(.width(3)) comparator_9 (.a(Rs), .b(Rd_WB), .eq(Rs3));  // open: gt, lt
  Comparator #(.width(3)) comparator_10 (.a(Rt), .b(Rd_ALU), .eq(Rt1));  // open: gt, lt
  Comparator #(.width(3)) comparator_11 (.a(Rt), .b(Rd_MEM), .eq(Rt2));  // open: gt, lt
  Comparator #(.width(3)) comparator_12 (.a(Rt), .b(Rd_WB), .eq(Rt3));  // open: gt, lt
  or or_1 (Rd1, comparator_1_gt, comparator_2_lt);
  or or_2 (Rd2, comparator_3_gt, comparator_4_lt);
  or or_3 (Rd3, comparator_5_gt, comparator_6_lt);
  and and_1 (selector1[0], RW_ALU, Rd1, Rs1);
  and and_2 (selector1[1], RW_MEM, Rd2, Rs2);
  and and_3 (selector1[2], RW_WB, Rd3, Rs3);
  and and_4 (selector2[0], RW_ALU, Rd1, Rt1);
  and and_5 (selector2[1], RW_MEM, Rd2, Rt2);
  and and_6 (selector2[2], RW_WB, Rd3, Rt3);
  or or_4 (or_4_out, Rs1, Rt1);
  and and_7 (stall, Memomry_Read, or_4_out);
  Multiplexer #(.select(3), .width(2), .enable("false")) multiplexer_1 (
    .in0(2'b00), .in1(2'b01), .in2(2'b10), .in3(2'b01), .in4(2'b11), .in5(2'b01), .in6(2'b10), .in7(2'b01),
    .out(forward_A), .sel(selector1));
  Multiplexer #(.select(3), .width(2), .enable("false")) multiplexer_2 (
    .in0(2'b00), .in1(2'b01), .in2(2'b10), .in3(2'b01), .in4(2'b11), .in5(2'b01), .in6(2'b10), .in7(2'b01),
    .out(forward_B), .sel(selector2));
endmodule
