// Logisim project CPU Pipline.circ as structural Verilog: 16 circuits, main circuit Pipline CPU
module instrction_memory (
  input  [11:0] in_1,
  output [15:0] out_2
);

  ROM #(.addrWidth(12), .dataWidth(16)) rom_1 (.addr(in_1), .data(out_2));  // open: sel

  // Notes on the sheet:
  //   Instruction_Memory
  //   contents of rom_1 (hex, n*v repeats v):
  //   a384 0 8354 0 373 0 2040 0 2081 0 20c2 0 890a 0 1921 0 1520 0 14f2 0 4182 0 1290 0 403b 0 3100 0
  //   4003 0 55c 0 1b68 0 403f 0 4e9 0 2040 0 2285 0 22c6 0 4e0 0 3100 0 4036
endmodule

module data_memory (
  input  [15:0] in_1,
  input  [15:0] in_2,
  input  in_3,
  input  in_4,
  input  in_5,
  output [15:0] out_6
);

  RAM #(.addrWidth(12), .dataWidth(16), .bus("separate")) ram_1 (
    .addr(in_1[11:0]), .din(in_2), .data(out_6), .str(in_3), .clk(in_5), .ld(in_4));  // open: sel, clr

  // Notes on the sheet:
  //   Data_Memory
endmodule

module CPU (
  input  in_1,
  input  in_2,
  output [15:0] out_3,
  output [2:0] out_4,
  output [15:0] out_5,
  output [3:0] out_6,
  output [3:0] out_7,
  output [2:0] out_8,
  output [11:0] out_9,
  output [1:0] out_10,
  output [15:0] out_11,
  output [15:0] out_12,
  output [15:0] out_13,
  output [15:0] out_14
);

  wire ALUSrc, clock_1_out, JumpCtrl, MemoryRead, MemoryReg, MemoryWrite;
  wire [1:0] JAL;
  wire [2:0] BrancheSelect, multiplexer_1_out, undriven;
  wire [11:0] main_1_p6;
  wire [15:0] bit_extender_1_out, bit_extender_2_out, bit_extender_3_out, data_memory_1_out_6,
       multiplexer_4_out, undriven_2, undriven_3;

  Clock clock_1 (.out(clock_1_out));
  assign bit_extender_1_out = {{4{1'b0}}, {out_9[11:3], out_4}};  // Bit_Extender bit_extender_1
  ll ll_1 (
    .Function(undriven), .out_10(JAL[0]), .out_11(MemoryReg), .out_12(JAL[1]), .out_14(ALUSrc),
    .out_15(MemoryWrite), .out_17(MemoryRead));  // open: OPcode, out_5, out_7, out_9, out_13, out_16, out_18, out_19, out_20, out_3, out_6, out_4, out_8
  // pc_main main_1: pin names not known; wires that end beside it: {out_9[11:3], out_4}, {out_9[11:3], out_4}, out_3, out_5, clock_1_out, main_1_p6, BrancheSelect, JumpCtrl, in_1
  assign bit_extender_2_out = {{4{1'b0}}, main_1_p6};  // Bit_Extender bit_extender_2
  Shifter #(.width(16)) shifter_1 (.in(bit_extender_1_out), .\dist (4'b0100), .out(out_14));
  instrction_memory instrction_memory_1 (.in_1(main_1_p6), .out_2({out_6, out_9[11:3], out_4}));
  Multiplexer #(.select(2), .width(3), .enable("false")) multiplexer_1 (
    .in0(out_9[8:6]), .in1(out_9[5:3]), .in2(3'b111), .in3(3'b001), .out(multiplexer_1_out), .sel(out_10));
  assign bit_extender_3_out = {{10{out_9[5]}}, {out_9[5:3], out_4}};  // Bit_Extender bit_extender_3
  Multiplexer #(.select(2), .width(16), .enable("false")) multiplexer_2 (
    .in0(multiplexer_4_out), .in2(bit_extender_2_out), .in3(out_14), .out(out_12), .sel(JAL));  // open: in1
  Multiplexer #(.width(16), .enable("false")) multiplexer_3 (
    .in0(out_5), .in1(bit_extender_3_out), .out(out_11), .sel(ALUSrc));
  data_memory data_memory_1 (
    .in_1(undriven_2), .in_2(out_5), .in_3(MemoryWrite), .in_4(MemoryRead), .out_6(data_memory_1_out_6),
    .in_5(clock_1_out));
  Multiplexer #(.width(16), .enable("false")) multiplexer_4 (
    .in0(undriven_2), .in1(data_memory_1_out_6), .out(multiplexer_4_out), .sel(MemoryReg));
  alu_main main_2 (.A(undriven_3));  // open: B, ALU_CONT, out_4
  // Reg_File reg_file_1: pin names not known

  assign out_9[2:0] = out_4;

  // Other names for the same wires on the sheet: DataLUI[11:0] = {out_9[11:3], out_4}; Funct[2:0] = out_4;
  //   Opcode[3:0] = out_6; RA[15:0] = out_3; RB[15:0] = out_5; RegDst[1:0] = out_10
endmodule

module jj (
  input  [5:0] in_1
);
endmodule

module ControlSrc (
  input  z,
  input  x,
  input  c,
  input  v,
  input  g,
  output JALR,
  output JumpCtrl,
  output H,
  output S,
  output RegWrite,
  output M,
  output N,
  output ALUSrc,
  output MemoryWrite,
  output MemoryRead,
  output MemoryReg
);

  wire and_1_out, and_2_out, and_3_out, and_4_out, and_5_out, and_6_out, and_7_out, and_8_out, and_9_out,
       and_10_out, and_11_out, and_12_out, and_13_out, and_14_out, and_15_out, and_16_out, and_17_out,
       and_18_out, and_19_out, and_20_out, and_21_out, and_22_out, and_23_out, and_24_out, and_26_out,
       and_27_out, and_28_out, and_29_out, and_31_out, and_32_out, not_1_out, not_2_out, not_3_out,
       not_4_out, not_5_out, not_6_out, not_7_out, not_8_out, not_9_out, not_10_out, not_11_out, not_12_out,
       not_13_out, not_14_out, not_15_out, not_16_out, not_18_out, not_19_out, not_20_out, not_21_out,
       or_1_out, or_5_out, or_6_out, or_7_out;

  not not_1 (not_1_out, z);
  not not_2 (not_2_out, z);
  not not_3 (not_3_out, c);
  not not_4 (not_4_out, c);
  not not_5 (not_5_out, c);
  not not_6 (not_6_out, g);
  not not_7 (not_7_out, z);
  not not_8 (not_8_out, v);
  not not_9 (not_9_out, c);
  not not_10 (not_10_out, g);
  not not_11 (not_11_out, x);
  not not_12 (not_12_out, c);
  not not_13 (not_13_out, g);
  not not_14 (not_14_out, c);
  not not_15 (not_15_out, x);
  not not_16 (not_16_out, c);
  not not_17 (MemoryRead, g);
  not not_18 (not_18_out, x);
  and and_1 (and_1_out, not_1_out, c);
  and and_2 (and_2_out, c, v);
  and and_3 (and_3_out, not_2_out, x);
  and and_4 (and_4_out, c, v);
  and and_5 (and_5_out, z, x);
  and and_6 (and_6_out, not_3_out, g);
  and and_7 (and_7_out, z, x);
  and and_8 (and_8_out, not_4_out, v);
  and and_9 (and_9_out, x, not_5_out);
  and and_10 (and_10_out, v, not_6_out);
  and and_11 (and_11_out, not_7_out, not_8_out);
  and and_12 (and_12_out, not_9_out, not_10_out);
  not not_19 (not_19_out, z);
  and and_13 (and_13_out, not_11_out, c);
  and and_14 (and_14_out, x, not_12_out);
  and and_15 (and_15_out, z, x);
  and and_16 (and_16_out, v, not_13_out);
  and and_17 (and_17_out, x, c);
  and and_18 (and_18_out, z, not_14_out);
  and and_19 (and_19_out, z, not_15_out);
  and and_20 (and_20_out, not_16_out, g);
  and and_21 (and_21_out, z, not_18_out);
  not not_20 (not_20_out, c);
  or or_1 (or_1_out, and_1_out, and_2_out);
  or or_2 (JALR, or_1_out, and_22_out);
  and and_22 (and_22_out, x, c);
  and and_23 (and_23_out, and_3_out, and_4_out);
  or or_3 (JumpCtrl, and_23_out, and_24_out);
  and and_24 (and_24_out, and_5_out, and_6_out);
  and and_25 (H, and_7_out, and_8_out);
  not not_21 (not_21_out, z);
  or or_4 (S, not_21_out, and_26_out);
  and and_26 (and_26_out, and_9_out, and_10_out);
  or or_5 (or_5_out, and_11_out, and_12_out);
  or or_6 (or_6_out, or_5_out, and_27_out);
  and and_27 (and_27_out, not_19_out, g);
  and and_28 (and_28_out, and_13_out, v);
  or or_7 (or_7_out, and_28_out, and_29_out);
  and and_29 (and_29_out, and_14_out, v);
  and and_30 (M, and_15_out, and_16_out);
  and and_31 (and_31_out, and_17_out, v);
  or or_8 (N, and_31_out, and_32_out);
  and and_32 (and_32_out, and_18_out, g);
  and and_33 (MemoryWrite, and_19_out, and_20_out);
  and and_34 (MemoryReg, and_21_out, not_20_out);
  or or_9 (RegWrite, or_6_out, or_7_out);

  assign ALUSrc = z;
endmodule

module ALUConrol (
  input  z,
  input  x,
  input  c,
  input  v,
  input  g,
  output A,
  output B,
  output C_2,
  output D
);

  wire and_1_out, and_4_out, and_5_out, and_6_out, and_7_out, and_8_out, and_9_out, and_10_out, and_11_out,
       and_12_out, not_1_out, not_2_out, not_3_out, not_4_out, not_5_out, not_6_out, not_7_out, not_8_out,
       not_9_out, not_10_out, or_1_out;

  not not_1 (not_1_out, x);
  not not_2 (not_2_out, z);
  not not_3 (not_3_out, z);
  not not_4 (not_4_out, x);
  not not_5 (not_5_out, z);
  and and_1 (and_1_out, z, not_1_out);
  not not_6 (not_6_out, c);
  not not_7 (not_7_out, c);
  not not_8 (not_8_out, v);
  not not_9 (not_9_out, g);
  and and_2 (B, not_2_out, c);
  and and_3 (C_2, not_3_out, v);
  not not_10 (not_10_out, z);
  and and_4 (and_4_out, not_4_out, c);
  and and_5 (and_5_out, v, g);
  and and_6 (and_6_out, not_5_out, x);
  or or_1 (or_1_out, and_6_out, and_7_out);
  and and_7 (and_7_out, and_1_out, not_6_out);
  and and_8 (and_8_out, z, not_7_out);
  and and_9 (and_9_out, and_8_out, and_10_out);
  and and_10 (and_10_out, not_8_out, not_9_out);
  and and_11 (and_11_out, not_10_out, g);
  or or_2 (D, and_11_out, and_12_out);
  and and_12 (and_12_out, and_4_out, and_5_out);
  or or_3 (A, or_1_out, and_9_out);
endmodule

module BranchSelect (
  input  z,
  input  x,
  input  c,
  input  v,
  input  g,
  output Q,
  output W,
  output E
);

  wire and_1_out, and_2_out, and_3_out, and_4_out, and_5_out, and_6_out, and_7_out, and_8_out, and_9_out,
       and_10_out, and_11_out, and_12_out, and_14_out, and_15_out, and_16_out, and_17_out, and_18_out,
       not_1_out, not_2_out, not_3_out, not_4_out, not_5_out, not_6_out, not_7_out, or_2_out;

  not not_1 (not_1_out, g);
  not not_2 (not_2_out, v);
  not not_3 (not_3_out, x);
  not not_4 (not_4_out, v);
  not not_5 (not_5_out, g);
  not not_6 (not_6_out, v);
  and and_1 (and_1_out, z, x);
  and and_2 (and_2_out, c, not_1_out);
  and and_3 (and_3_out, z, x);
  and and_4 (and_4_out, c, v);
  and and_5 (and_5_out, z, c);
  and and_6 (and_6_out, not_2_out, g);
  and and_7 (and_7_out, z, not_3_out);
  and and_8 (and_8_out, not_4_out, not_5_out);
  and and_9 (and_9_out, z, x);
  and and_10 (and_10_out, c, not_6_out);
  not not_7 (not_7_out, g);
  and and_11 (and_11_out, and_1_out, and_2_out);
  or or_1 (Q, and_11_out, and_12_out);
  and and_12 (and_12_out, and_3_out, and_4_out);
  and and_13 (W, and_5_out, and_6_out);
  and and_14 (and_14_out, and_7_out, and_8_out);
  or or_2 (or_2_out, and_14_out, and_15_out);
  and and_15 (and_15_out, and_9_out, and_10_out);
  and and_16 (and_16_out, z, x);
  and and_17 (and_17_out, and_16_out, and_18_out);
  and and_18 (and_18_out, c, not_7_out);
  or or_3 (E, or_2_out, and_17_out);
endmodule

module BranchSelect1 (
  input  z,
  input  x,
  input  c,
  input  v,
  input  g,
  output Q,
  output W,
  output E
);

  wire and_1_out, and_2_out, and_3_out, and_4_out, and_5_out, and_6_out, and_7_out, not_1_out, not_2_out,
       not_3_out, not_4_out, not_5_out, not_6_out, not_7_out, not_8_out, not_9_out;

  not not_1 (not_1_out, g);
  not not_2 (not_2_out, x);
  not not_3 (not_3_out, v);
  not not_4 (not_4_out, v);
  not not_5 (not_5_out, x);
  not not_6 (not_6_out, v);
  not not_7 (not_7_out, g);
  not not_8 (not_8_out, v);
  not not_9 (not_9_out, g);
  and and_1 (and_1_out, z, x, c, not_1_out);
  and and_2 (and_2_out, z, x, c, v);
  and and_3 (and_3_out, z, not_2_out, not_3_out, g);
  and and_4 (and_4_out, z, x, c, not_4_out);
  and and_5 (and_5_out, z, not_5_out, not_6_out, not_7_out);
  and and_6 (and_6_out, z, x, c, not_8_out, g);
  and and_7 (and_7_out, z, x, c, v, not_9_out);
  or or_1 (Q, and_1_out, and_2_out);
  or or_2 (W, and_3_out, and_4_out);
  or or_3 (E, and_5_out, and_6_out, and_7_out);
endmodule

module Pipline_CPU (
);

  wire ALUSrc, ALUSrc_1, Br, Clock, JALR, JumpCtrl, Kill1, LUI1, LUI2, LUI3, LUI4, MemoryRead, MemoryRead_2,
       MemoryRead_3, MemoryReg, MemoryReg_1, MemoryWrite, MemoryWrite_1, RegWrite, RegWrite_1, RegWrite_ALU,
       RegWrite_MEM, Stall;
  wire [1:0] Forward_Rs, Forward_Rt, JAL, JAL_1, RegDst;
  wire [2:0] BrancheSelect, Rd_0, Rd_1, Rd_2, Rd_3;
  wire [3:0] ALU_CONT, ALU_CONT_1, Opcode;
  wire [4:0] ex_mem_1_out_9;
  wire [7:0] id_ex_1_out_12;
  wire [11:0] DataLUI, multiplexer_1_out, Next_PC, PC;
  wire [15:0] ALU_data, ALU_Res, bit_extender_1_out, bit_extender_2_out, bit_extender_3_out, Bus_A, Bus_B,
       Bus_B_1, dataWrite, immm16, LUI_Res1, LUI_Res_2, LUI_Res_3, LUI_Res_4, main_2_out_4, Mem_data,
       multiplexer_2_out, multiplexer_4_out, multiplexer_7_out, multiplexer_10_out, Next_PC1, Next_PC_2,
       Next_PC_3, Next_PC_4, RA, ram_1_data, RB, reg_file_1_read_data_1, reg_file_1_read_data_2, rom_1_data,
       WB_data;

  Multiplexer #(.width(12), .enable("false")) multiplexer_1 (
    .in0(DataLUI), .in1(RA[11:0]), .out(multiplexer_1_out), .sel(JALR));
  assign bit_extender_1_out = {{4{1'b0}}, DataLUI};  // Bit_Extender bit_extender_1
  pc_main main_1 (
    .jump_or_branch_value(multiplexer_1_out), .in_4(RA), .in_6(RB), .pc(PC), .jump(JumpCtrl),
    .in_7(BrancheSelect), .in_5(Clock), .out_8(Next_PC), .out_10(Br), .in_3(Stall));
  Shifter #(.width(16)) shifter_1 (.in(bit_extender_1_out), .\dist (4'b0100), .out(LUI_Res1));
  Clock clock_1 (.out(Clock));
  ROM #(.addrWidth(12), .dataWidth(16)) rom_1 (.addr(PC), .data(rom_1_data));  // open: sel
  and and_1 (LUI1, RegDst[0], RegDst[1]);
  assign bit_extender_2_out = {{4{1'b0}}, Next_PC};  // Bit_Extender bit_extender_2
  Multiplexer #(.width(16), .enable("false")) multiplexer_2 (
    .in0(rom_1_data), .in1({16{1'b0}}), .out(multiplexer_2_out), .sel(Kill1));
  Multiplexer #(.select(2), .width(3), .enable("false")) multiplexer_3 (
    .in0(DataLUI[8:6]), .in1(DataLUI[5:3]), .in2(3'b111), .in3(3'b001), .out(Rd_0), .sel(RegDst));
  IF_ID if_id_1 (
    .in_2(multiplexer_2_out), .in_4(Clock), .out_6({Opcode, DataLUI}), .in_3(Stall),
    .in_1(bit_extender_2_out), .out_5(Next_PC1));
  Reg_File reg_file_1 (
    .register_write(Rd_3), .reg_write(RegWrite_1), .write_data(multiplexer_4_out),
    .read_register_1(DataLUI[11:9]), .read_data_1(reg_file_1_read_data_1),
    .read_data_2(reg_file_1_read_data_2), .read_register_2(DataLUI[8:6]), .clock(Clock));
  Multiplexer #(.select(2), .width(16), .enable("false")) multiplexer_4 (
    .in0(dataWrite), .in1(Next_PC_4), .in2(LUI_Res_4), .out(multiplexer_4_out), .sel(JAL_1));  // open: in3
  Multiplexer #(.select(2), .width(16), .enable("false")) multiplexer_5 (
    .in0(reg_file_1_read_data_2), .in1(ALU_data), .in2(Mem_data), .in3(WB_data), .out(RB), .sel(Forward_Rt));
  Multiplexer #(.select(2), .width(16), .enable("false")) multiplexer_6 (
    .in0(reg_file_1_read_data_1), .in1(ALU_data), .in2(Mem_data), .in3(WB_data), .out(RA), .sel(Forward_Rs));
  Killer_Circuit killer_circuit_1 (.in_2(Br), .in_1(JumpCtrl), .out_3(Kill1));
  assign bit_extender_3_out = {{10{DataLUI[5]}}, DataLUI[5:0]};  // Bit_Extender bit_extender_3
  ID_EX id_ex_1 (
    .in_1({MemoryReg, MemoryRead, MemoryWrite, ALUSrc, JAL[0], JAL[1], RegWrite, 2'b00}), .in_3(ALU_CONT),
    .in_4(LUI_Res1), .in_5(Next_PC1), .in_6(bit_extender_3_out), .in_7(RA), .in_8(RB), .in_10(Rd_0),
    .out_12({MemoryRead_3, id_ex_1_out_12[7:6], ALUSrc_1, id_ex_1_out_12[4:3], RegWrite_ALU, id_ex_1_out_12[1:0]}),
    .out_13(ALU_CONT_1), .out_14(LUI_Res_2), .out_15(Next_PC_2), .out_16(immm16), .out_17(Bus_A),
    .out_18(Bus_B), .out_20(Rd_1), .in_11(Clock), .in_9(LUI1), .out_19(LUI2), .in_2(Stall));
  alu_main main_2 (.A(Bus_A), .B(multiplexer_7_out), .ALU_CONT(ALU_CONT_1), .out_4(main_2_out_4));
  Multiplexer #(.width(16), .enable("false")) multiplexer_7 (
    .in0(Bus_B), .in1(immm16), .out(multiplexer_7_out), .sel(ALUSrc_1));
  Control_Hazard control_hazard_1 (
    .Rd_ALU(Rd_1), .RW_ALU(RegWrite_ALU), .Rd_MEM(Rd_2), .RW_MEM(RegWrite_MEM), .RW_WB(RegWrite_1),
    .Rd_WB(Rd_3), .Rs(DataLUI[11:9]), .Rt(DataLUI[8:6]), .Memomry_Read(MemoryRead_3), .forward_A(Forward_Rs),
    .forward_B(Forward_Rt), .stall(Stall));
  Multiplexer #(.width(16), .enable("false")) multiplexer_8 (
    .in0(main_2_out_4), .in1(LUI_Res_2), .out(ALU_data), .sel(LUI2));
  EX_MEM ex_mem_1 (
    .in_1({MemoryRead_3, id_ex_1_out_12[7:6], id_ex_1_out_12[4:3], RegWrite_ALU, id_ex_1_out_12[1:0]}),
    .in_2(LUI_Res_2), .in_3(Next_PC_2), .in_5(Bus_B), .in_6(Rd_1), .in_7(LUI2),
    .out_9({MemoryReg_1, MemoryRead_2, MemoryWrite_1, ex_mem_1_out_9[4:3], RegWrite_MEM, ex_mem_1_out_9[1:0]}),
    .out_10(LUI_Res_3), .out_11(Next_PC_3), .out_13(Bus_B_1), .out_14(Rd_2), .out_15(LUI3), .in_8(Clock),
    .in_4(main_2_out_4), .out_12(ALU_Res));
  RAM #(.addrWidth(12), .dataWidth(16), .bus("separate")) ram_1 (
    .addr(ALU_Res[11:0]), .din(Bus_B_1), .data(ram_1_data), .str(MemoryWrite_1), .clk(Clock),
    .ld(MemoryRead_2));  // open: sel, clr
  ll ll_1 (
    .Function(DataLUI[2:0]), .OPcode(Opcode), .out_5(JALR), .out_7(JumpCtrl), .out_9(RegDst[1]),
    .out_10(RegDst[0]), .out_11(RegWrite), .out_12(JAL[1]), .out_13(JAL[0]), .out_14(ALUSrc),
    .out_15(MemoryWrite), .out_16(MemoryRead), .out_17(MemoryReg), .out_18(BrancheSelect[2]),
    .out_19(BrancheSelect[1]), .out_20(BrancheSelect[0]), .out_3(ALU_CONT[3]), .out_6(ALU_CONT[1]),
    .out_4(ALU_CONT[2]), .out_8(ALU_CONT[0]));
  Multiplexer #(.width(16), .enable("false")) multiplexer_9 (
    .in0(multiplexer_10_out), .in1(LUI_Res_3), .out(Mem_data), .sel(LUI3));
  Multiplexer #(.width(16), .enable("false")) multiplexer_10 (
    .in0(ALU_Res), .in1(ram_1_data), .out(multiplexer_10_out), .sel(MemoryReg_1));
  MEM_WB mem_wb_1 (
    .in_1({ex_mem_1_out_9[4:3], RegWrite_MEM}), .in_2(LUI_Res_3), .in_3(Next_PC_3),
    .in_4(multiplexer_10_out), .in_5(Rd_2), .in_6(LUI3), .out_8({JAL_1[0], JAL_1[1], RegWrite_1}),
    .out_9(LUI_Res_4), .out_10(Next_PC_4), .out_11(dataWrite), .out_12(Rd_3), .out_13(LUI4), .in_7(Clock));
  Multiplexer #(.width(16), .enable("false")) multiplexer_11 (
    .in0(dataWrite), .in1(LUI_Res_4), .out(WB_data), .sel(LUI4));

  // Other names for the same wires on the sheet: Funct[2:0] = DataLUI[2:0]; imm6[5:0] = DataLUI[5:0];
  //   imm12[11:0] = DataLUI; Rd[2:0] = DataLUI[5:3]; Rt[2:0] = DataLUI[8:6]; Rs[2:0] = DataLUI[11:9]

  // Notes on the sheet:
  //   Instruction_Memory
  //   contents of rom_1 (hex, n*v repeats v):
  //   a384 0 8354 0 35b 0 2040 0 2081 0 20c2 0 890a 0 1921 0 1520 0 14f2 0 4c02 0 1290 0 403b 0 3100 0
  //   b024 0 55c 0 1b68 0 403f 0 4e9 0 2040 0 2285 0 22c6 0 4e0 0 3100 0 1e06
  //   Data_Memory
endmodule

module Single_cycle_CPU (
  output [15:0] out_1
);

  wire ALUSrc, Clock, JALR, JumpCtrl, MemoryRead, MemoryReg, MemoryWrite, RegWrite;
  wire [1:0] JAL, RegDst;
  wire [2:0] BrancheSelect, multiplexer_2_out;
  wire [3:0] ALU_CONT, Opcode;
  wire [11:0] DataLUI, multiplexer_1_out, Next_PC, PC;
  wire [15:0] ALU_Res, bit_extender_1_out, bit_extender_2_out, bit_extender_3_out, dataWrite, LUI_Res,
       multiplexer_4_out, RA, ram_1_data, RB;

  Multiplexer #(.width(12), .enable("false")) multiplexer_1 (
    .in0(DataLUI), .in1(RA[11:0]), .out(multiplexer_1_out), .sel(JALR));
  assign bit_extender_1_out = {{4{1'b0}}, DataLUI};  // Bit_Extender bit_extender_1
  pc_main main_1 (
    .jump_or_branch_value(multiplexer_1_out), .in_4(RA), .in_6(RB), .pc(PC), .jump(JumpCtrl),
    .in_7(BrancheSelect), .in_5(Clock), .out_8(Next_PC));  // open: out_10, in_3
  Shifter #(.width(16)) shifter_1 (.in(bit_extender_1_out), .\dist (4'b0100), .out(LUI_Res));
  Clock clock_1 (.out(Clock));
  ROM #(.addrWidth(12), .dataWidth(16)) rom_1 (.addr(PC), .data({Opcode, DataLUI}));  // open: sel
  ll ll_1 (
    .Function(DataLUI[2:0]), .OPcode(Opcode), .out_5(JALR), .out_7(JumpCtrl), .out_9(RegDst[1]),
    .out_10(RegDst[0]), .out_11(RegWrite), .out_12(JAL[1]), .out_13(JAL[0]), .out_14(ALUSrc),
    .out_15(MemoryWrite), .out_16(MemoryRead), .out_17(MemoryReg), .out_18(BrancheSelect[2]),
    .out_19(BrancheSelect[1]), .out_20(BrancheSelect[0]), .out_3(ALU_CONT[3]), .out_6(ALU_CONT[1]),
    .out_4(ALU_CONT[2]), .out_8(ALU_CONT[0]));
  Multiplexer #(.select(2), .width(3), .enable("false")) multiplexer_2 (
    .in0(DataLUI[8:6]), .in1(DataLUI[5:3]), .in2(3'b111), .in3(3'b001), .out(multiplexer_2_out), .sel(RegDst));
  Reg_File reg_file_1 (
    .register_write(multiplexer_2_out), .reg_write(RegWrite), .write_data(out_1),
    .read_register_1(DataLUI[11:9]), .read_data_1(RA), .read_data_2(RB), .read_register_2(DataLUI[8:6]),
    .clock(Clock));
  assign bit_extender_2_out = {{4{1'b0}}, Next_PC};  // Bit_Extender bit_extender_2
  Multiplexer #(.select(2), .width(16), .enable("false")) multiplexer_3 (
    .in0(dataWrite), .in1(bit_extender_2_out), .in2(LUI_Res), .out(out_1), .sel(JAL));  // open: in3
  assign bit_extender_3_out = {{10{DataLUI[5]}}, DataLUI[5:0]};  // Bit_Extender bit_extender_3
  Multiplexer #(.width(16), .enable("false")) multiplexer_4 (
    .in0(RB), .in1(bit_extender_3_out), .out(multiplexer_4_out), .sel(ALUSrc));
  alu_main main_2 (.A(RA), .B(multiplexer_4_out), .ALU_CONT(ALU_CONT), .out_4(ALU_Res));
  RAM #(.addrWidth(12), .dataWidth(16), .bus("separate")) ram_1 (
    .addr(ALU_Res[11:0]), .din(RB), .data(ram_1_data), .str(MemoryWrite), .clk(Clock), .ld(MemoryRead));  // open: sel, clr
  Multiplexer #(.width(16), .enable("false")) multiplexer_5 (
    .in0(ALU_Res), .in1(ram_1_data), .out(dataWrite), .sel(MemoryReg));

  // Other names for the same wires on the sheet: Funct[2:0] = DataLUI[2:0]; imm6[5:0] = DataLUI[5:0];
  //   imm12[11:0] = DataLUI; Rd[2:0] = DataLUI[5:3]; Rt[2:0] = DataLUI[8:6]; Rs[2:0] = DataLUI[11:9]

  // Notes on the sheet:
  //   Instruction_Memory
  //   contents of rom_1 (hex, n*v repeats v):
  //   a384 0 8354 0 35b 0 2040 0 2081 0 20c2 0 890a 0 1921 0 1520 0 14f2 0 4c02 0 1290 0 403b 0 3100 0
  //   b024 0 55c 0 1b68 0 403f 0 4e9 0 2040 0 2285 0 22c6 0 4e0 0 3100 0 1e06
  //   Data_Memory
endmodule

module Next_PC (
  input  [15:0] in_1,
  input  [15:0] in_2,
  input  in_3,
  output [15:0] out_4,
  output [15:0] out_5
);

  Register #(.width(16)) R9 (.D(in_1), .Q(out_4), .clk(in_3));  // open: en, clr
  Register #(.width(16)) R9_2 (.D(in_2), .Q(out_5), .clk(in_3));  // open: en, clr
endmodule

module IF_ID (
  input  [15:0] in_1,
  input  [15:0] in_2,
  input  in_3,
  input  in_4,
  output [15:0] out_5,
  output [15:0] out_6
);

  wire not_1_out;

  not not_1 (not_1_out, in_3);
  Register #(.width(16)) R3 (.D(in_1), .Q(out_5), .clk(in_4));  // open: en, clr
  Register #(.width(16)) R3_2 (.D(in_2), .en(not_1_out), .Q(out_6), .clk(in_4));  // open: clr
endmodule

// RA
module ID_EX (
  input  [8:0] in_1,
  input  in_2,
  input  [3:0] in_3,
  input  [15:0] in_4,
  input  [15:0] in_5,
  input  [15:0] in_6,
  input  [15:0] in_7,
  input  [15:0] in_8,
  input  in_9,
  input  [2:0] in_10,
  input  in_11,
  output [8:0] out_12,
  output [3:0] out_13,
  output [15:0] out_14,
  output [15:0] out_15,
  output [15:0] out_16,
  output [15:0] out_17,
  output [15:0] out_18,
  output out_19,
  output [2:0] out_20
);

  wire [8:0] multiplexer_1_out;

  Multiplexer #(.width(9), .enable("false")) multiplexer_1 (
    .in0(in_1), .in1({9{1'b0}}), .out(multiplexer_1_out), .sel(in_2));
  Register #(.width(4)) R3 (.D(in_3), .Q(out_13), .clk(in_11));  // open: en, clr
  Register #(.width(16)) R3_2 (.D(in_4), .Q(out_14), .clk(in_11));  // open: en, clr
  Register #(.width(16)) R3_3 (.D(in_5), .Q(out_15), .clk(in_11));  // open: en, clr
  Register #(.width(16)) R3_4 (.D(in_6), .Q(out_16), .clk(in_11));  // open: en, clr
  Register #(.width(16)) R3_5 (.D(in_7), .Q(out_17), .clk(in_11));  // open: en, clr
  Register #(.width(16)) R3_6 (.D(in_8), .Q(out_18), .clk(in_11));  // open: en, clr
  Register #(.width(1)) R3_7 (.D(in_9), .Q(out_19), .clk(in_11));  // open: en, clr
  Register #(.width(3)) R3_8 (.D(in_10), .Q(out_20), .clk(in_11));  // open: en, clr
  Register #(.width(9)) R3_9 (.D(multiplexer_1_out), .Q(out_12), .clk(in_11));  // open: en, clr
endmodule

module Killer_Circuit (
  input  in_1,
  input  in_2,
  output out_3
);

  wire and_1_out, not_1_out;

  or or_1 (out_3, in_2, and_1_out);
  not not_1 (not_1_out, in_2);
  and and_1 (and_1_out, not_1_out, in_1);

  // Notes on the sheet:
  //   Killer
  //   Beq
  //   J
endmodule

module EX_MEM (
  input  [7:0] in_1,
  input  [15:0] in_2,
  input  [15:0] in_3,
  input  [15:0] in_4,
  input  [15:0] in_5,
  input  [2:0] in_6,
  input  in_7,
  input  in_8,
  output [7:0] out_9,
  output [15:0] out_10,
  output [15:0] out_11,
  output [15:0] out_12,
  output [15:0] out_13,
  output [2:0] out_14,
  output out_15
);

  Register R3 (.D(in_1), .Q(out_9), .clk(in_8));  // open: en, clr
  Register #(.width(16)) R3_2 (.D(in_2), .Q(out_10), .clk(in_8));  // open: en, clr
  Register #(.width(16)) R3_3 (.D(in_3), .Q(out_11), .clk(in_8));  // open: en, clr
  Register #(.width(16)) R3_4 (.D(in_4), .Q(out_12), .clk(in_8));  // open: en, clr
  Register #(.width(16)) R3_5 (.D(in_5), .Q(out_13), .clk(in_8));  // open: en, clr
  Register #(.width(3)) R3_6 (.D(in_6), .Q(out_14), .clk(in_8));  // open: en, clr
  Register #(.width(1)) R3_7 (.D(in_7), .Q(out_15), .clk(in_8));  // open: en, clr
endmodule

module MEM_WB (
  input  [2:0] in_1,
  input  [15:0] in_2,
  input  [15:0] in_3,
  input  [15:0] in_4,
  input  [2:0] in_5,
  input  in_6,
  input  in_7,
  output [2:0] out_8,
  output [15:0] out_9,
  output [15:0] out_10,
  output [15:0] out_11,
  output [2:0] out_12,
  output out_13
);

  Register #(.width(3)) R3 (.D(in_1), .Q(out_8), .clk(in_7));  // open: en, clr
  Register #(.width(16)) R3_2 (.D(in_2), .Q(out_9), .clk(in_7));  // open: en, clr
  Register #(.width(16)) R3_3 (.D(in_3), .Q(out_10), .clk(in_7));  // open: en, clr
  Register #(.width(16)) R3_4 (.D(in_4), .Q(out_11), .clk(in_7));  // open: en, clr
  Register #(.width(3)) R3_5 (.D(in_5), .Q(out_12), .clk(in_7));  // open: en, clr
  Register #(.width(1)) R3_6 (.D(in_6), .Q(out_13), .clk(in_7));  // open: en, clr
endmodule
