// Logisim project LastCntrol3.circ as structural Verilog: 3 circuits, main circuit ll
module ll (
  input  [2:0] Function,
  input  [3:0] OPcode,
  output out_3,
  output out_4,
  output out_5,
  output out_6,
  output out_7,
  output out_8,
  output out_9,
  output out_10,
  output out_11,
  output out_12,
  output out_13,
  output out_14,
  output out_15,
  output out_16,
  output out_17,
  output out_18,
  output out_19,
  output out_20
);

  wire nor_1_out, nor_2_out, not_1_out;
  wire [4:0] bit_extender_1_out, multiplexer_1_out, multiplexer_2_out;

  assign bit_extender_1_out = {{1{1'b1}}, OPcode};  // Bit_Extender bit_extender_1
  not not_1 (not_1_out, OPcode[0]);
  nor nor_1 (nor_1_out, not_1_out, OPcode[1], OPcode[2], OPcode[3]);
  nor nor_2 (nor_2_out, OPcode[0], OPcode[1], OPcode[2], OPcode[3]);
  Multiplexer #(.width(5), .enable("false")) multiplexer_1 (
    .in0(bit_extender_1_out), .in1({2'b00, Function}), .out(multiplexer_1_out), .sel(nor_2_out));
  Multiplexer #(.width(5), .enable("false")) multiplexer_2 (
    .in0(multiplexer_1_out), .in1({2'b01, Function}), .out(multiplexer_2_out), .sel(nor_1_out));
  ALUConrol aluconrol_1 (
    .z(multiplexer_2_out[4]), .x(multiplexer_2_out[3]), .c(multiplexer_2_out[2]), .v(multiplexer_2_out[1]),
    .g(multiplexer_2_out[0]), .A(out_3), .B(out_4), .C_2(out_6), .D(out_8));
  ControlSrc33 controlsrc33_1 (
    .z(multiplexer_2_out[4]), .x(multiplexer_2_out[3]), .c(multiplexer_2_out[2]), .v(multiplexer_2_out[1]),
    .g(multiplexer_2_out[0]), .JALR(out_5), .JumpCtrl(out_7), .H(out_9), .S(out_10), .RegWrite(out_11),
    .M(out_12), .N(out_13), .ALUSrc(out_14), .MemoryWrite(out_15), .MemoryRead(out_16), .MemoryReg(out_17));
  BranchSelect1 branchselect1_1 (
    .z(multiplexer_2_out[4]), .x(multiplexer_2_out[3]), .c(multiplexer_2_out[2]), .v(multiplexer_2_out[1]),
    .g(multiplexer_2_out[0]), .Q(out_18), .W(out_19), .E(out_20));
endmodule

module ControlSrc (
  input  z,
  input  x,
  input  c,
  input  v,
  input  g,
  output JALR,
  output JumpCtrl,
  output H,
  output S,
  output RegWrite,
  output M,
  output N,
  output ALUSrc,
  output MemoryWrite,
  output MemoryRead,
  output MemoryReg
);

  wire and_1_out, and_2_out, and_3_out, and_4_out, and_5_out, and_6_out, and_7_out, and_8_out, and_9_out,
       and_10_out, and_11_out, and_12_out, and_13_out, and_14_out, and_15_out, and_16_out, and_17_out,
       and_18_out, and_19_out, and_20_out, and_21_out, and_22_out, and_23_out, and_24_out, and_26_out,
       and_27_out, and_28_out, and_29_out, and_31_out, and_32_out, not_1_out, not_2_out, not_3_out,
       not_4_out, not_5_out, not_6_out, not_7_out, not_8_out, not_9_out, not_10_out, not_11_out, not_12_out,
       not_13_out, not_14_out, not_15_out, not_16_out, not_18_out, not_19_out, not_20_out, not_21_out,
       or_1_out, or_5_out, or_6_out, or_7_out;

  not not_1 (not_1_out, z);
  not not_2 (not_2_out, z);
  not not_3 (not_3_out, c);
  not not_4 (not_4_out, c);
  not not_5 (not_5_out, c);
  not not_6 (not_6_out, g);
  not not_7 (not_7_out, z);
  not not_8 (not_8_out, v);
  not not_9 (not_9_out, c);
  not not_10 (not_10_out, g);
  not not_11 (not_11_out, x);
  not not_12 (not_12_out, c);
  not not_13 (not_13_out, g);
  not not_14 (not_14_out, c);
  not not_15 (not_15_out, x);
  not not_16 (not_16_out, c);
  not not_17 (MemoryRead, g);
  not not_18 (not_18_out, x);
  and and_1 (and_1_out, not_1_out, c);
  and and_2 (and_2_out, c, v);
  and and_3 (and_3_out, not_2_out, x);
  and and_4 (and_4_out, c, v);
  and and_5 (and_5_out, z, x);
  and and_6 (and_6_out, not_3_out, g);
  and and_7 (and_7_out, z, x);
  and and_8 (and_8_out, not_4_out, v);
  and and_9 (and_9_out, x, not_5_out);
  and and_10 (and_10_out, v, not_6_out);
  and and_11 (and_11_out, not_7_out, not_8_out);
  and and_12 (and_12_out, not_9_out, not_10_out);
  not not_19 (not_19_out, z);
  and and_13 (and_13_out, not_11_out, c);
  and and_14 (and_14_out, x, not_12_out);
  and and_15 (and_15_out, z, x);
  and and_16 (and_16_out, v, not_13_out);
  and and_17 (and_17_out, x, c);
  and and_18 (and_18_out, z, not_14_out);
  and and_19 (and_19_out, z, not_15_out);
  and and_20 (and_20_out, not_16_out, g);
  and and_21 (and_21_out, z, not_18_out);
  not not_20 (not_20_out, c);
  or or_1 (or_1_out, and_1_out, and_2_out);
  or or_2 (JALR, or_1_out, and_22_out);
  and and_22 (and_22_out, x, c);
  and and_23 (and_23_out, and_3_out, and_4_out);
  or or_3 (JumpCtrl, and_23_out, and_24_out);
  and and_24 (and_24_out, and_5_out, and_6_out);
  and and_25 (H, and_7_out, and_8_out);
  not not_21 (not_21_out, z);
  or or_4 (S, not_21_out, and_26_out);
  and and_26 (and_26_out, and_9_out, and_10_out);
  or or_5 (or_5_out, and_11_out, and_12_out);
  or or_6 (or_6_out, or_5_out, and_27_out);
  and and_27 (and_27_out, not_19_out, g);
  and and_28 (and_28_out, and_13_out, v);
  or or_7 (or_7_out, and_28_out, and_29_out);
  and and_29 (and_29_out, and_14_out, v);
  and and_30 (M, and_15_out, and_16_out);
  and and_31 (and_31_out, and_17_out, v);
  or or_8 (N, and_31_out, and_32_out);
  and and_32 (and_32_out, and_18_out, g);
  and and_33 (MemoryWrite, and_19_out, and_20_out);
  and and_34 (MemoryReg, and_21_out, not_20_out);
  or or_9 (RegWrite, or_6_out, or_7_out);

  assign ALUSrc = z;
endmodule

module ControlSrc33 (
  input  z,
  input  x,
  input  c,
  input  v,
  input  g,
  output JALR,
  output JumpCtrl,
  output H,
  output S,
  output RegWrite,
  output M,
  output N,
  output ALUSrc,
  output MemoryWrite,
  output MemoryRead,
  output MemoryReg
);

  wire and_1_out, and_2_out, and_3_out, and_4_out, and_5_out, and_6_out, and_7_out, and_8_out, and_9_out,
       and_10_out, and_11_out, and_12_out, and_13_out, and_14_out, and_15_out, and_16_out, and_17_out,
       and_18_out, and_19_out, and_20_out, and_21_out, and_22_out, and_23_out, and_24_out, and_26_out,
       and_27_out, and_28_out, and_29_out, and_31_out, and_32_out, not_1_out, not_2_out, not_3_out,
       not_4_out, not_5_out, not_6_out, not_7_out, not_8_out, not_9_out, not_10_out, not_11_out, not_12_out,
       not_13_out, not_14_out, not_15_out, not_16_out, not_18_out, not_19_out, not_20_out, not_21_out,
       or_1_out, or_5_out, or_6_out, or_7_out;

  not not_1 (not_1_out, z);
  not not_2 (not_2_out, z);
  not not_3 (not_3_out, c);
  not not_4 (not_4_out, c);
  not not_5 (not_5_out, c);
  not not_6 (not_6_out, g);
  not not_7 (not_7_out, z);
  not not_8 (not_8_out, v);
  not not_9 (not_9_out, c);
  not not_10 (not_10_out, g);
  not not_11 (not_11_out, x);
  not not_12 (not_12_out, c);
  not not_13 (not_13_out, g);
  not not_14 (not_14_out, c);
  not not_15 (not_15_out, x);
  not not_16 (not_16_out, c);
  not not_17 (MemoryRead, g);
  not not_18 (not_18_out, x);
  and and_1 (and_1_out, not_1_out, c);
  and and_2 (and_2_out, c, v);
  and and_3 (and_3_out, not_2_out, x);
  and and_4 (and_4_out, c, v);
  and and_5 (and_5_out, z, x);
  and and_6 (and_6_out, not_3_out, g);
  and and_7 (and_7_out, z, x);
  and and_8 (and_8_out, not_4_out, v);
  and and_9 (and_9_out, x, not_5_out);
  and and_10 (and_10_out, v, not_6_out);
  and and_11 (and_11_out, not_7_out, not_8_out);
  and and_12 (and_12_out, not_9_out, not_10_out);
  not not_19 (not_19_out, z);
  and and_13 (and_13_out, not_11_out, c);
  and and_14 (and_14_out, x, not_12_out);
  and and_15 (and_15_out, z, x);
  and and_16 (and_16_out, v, not_13_out);
  and and_17 (and_17_out, x, c);
  and and_18 (and_18_out, z, not_14_out);
  and and_19 (and_19_out, z, not_15_out);
  and and_20 (and_20_out, not_16_out, g);
  and and_21 (and_21_out, z, not_18_out);
  not not_20 (not_20_out, c);
  or or_1 (or_1_out, and_1_out, and_2_out);
  or or_2 (JALR, or_1_out, and_22_out);
  and and_22 (and_22_out, x, c);
  and and_23 (and_23_out, and_3_out, and_4_out);
  or or_3 (JumpCtrl, and_23_out, and_24_out);
  and and_24 (and_24_out, and_5_out, and_6_out);
  and and_25 (H, and_7_out, and_8_out);
  not not_21 (not_21_out, z);
  or or_4 (S, not_21_out, and_26_out);
  and and_26 (and_26_out, and_9_out, and_10_out);
  or or_5 (or_5_out, and_11_out, and_12_out);
  or or_6 (or_6_out, or_5_out, and_27_out);
  and and_27 (and_27_out, not_19_out, g);
  and and_28 (and_28_out, and_13_out, v);
  or or_7 (or_7_out, and_28_out, and_29_out);
  and and_29 (and_29_out, and_14_out, v);
  and and_30 (M, and_15_out, and_16_out);
  and and_31 (and_31_out, and_17_out, v);
  or or_8 (N, and_31_out, and_32_out);
  and and_32 (and_32_out, and_18_out, g);
  and and_33 (MemoryWrite, and_19_out, and_20_out);
  and and_34 (MemoryReg, and_21_out, not_20_out);
  or or_9 (RegWrite, or_6_out, or_7_out);

  assign ALUSrc = z;
endmodule
