// Logisim project reg.file.circ as structural Verilog: 1 circuit, main circuit Reg_File
module Reg_File (
  input  [2:0] read_register_1,
  input  [2:0] register_write,
  input  [2:0] read_register_2,
  input  reg_write,
  input  [15:0] write_data,
  input  clock,
  output [15:0] read_data_1,
  output [15:0] read_data_2
);

  wire and_1_out, and_2_out, and_3_out, and_4_out, and_5_out, and_6_out, and_7_out, and_8_out,
       decoder_1_out0, decoder_1_out1, decoder_1_out2, decoder_1_out3, decoder_1_out4, decoder_1_out5,
       decoder_1_out6, decoder_1_out7;
  wire [15:0] R0_q, R1_q, R2_q, R3_q, R4_q, R5_q, R6_q, R7_q;

  Decoder #(.select(3), .enable("false")) decoder_1 (
    .out0(decoder_1_out0), .out1(decoder_1_out1), .out2(decoder_1_out2), .out3(decoder_1_out3),
    .out4(decoder_1_out4), .out5(decoder_1_out5), .out6(decoder_1_out6), .out7(decoder_1_out7),
    .sel(register_write));
  and and_1 (and_1_out, decoder_1_out0, 1'b0);
  and and_2 (and_2_out, decoder_1_out1, reg_write);
  and and_3 (and_3_out, decoder_1_out2, reg_write);
  and and_4 (and_4_out, decoder_1_out3, reg_write);
  and and_5 (and_5_out, decoder_1_out4, reg_write);
  and and_6 (and_6_out, decoder_1_out5, reg_write);
  and and_7 (and_7_out, decoder_1_out6, reg_write);
  and and_8 (and_8_out, decoder_1_out7, reg_write);
  Register #(.width(16)) R0 (.D(write_data), .en(and_1_out), .Q(R0_q), .clk(clock), .clr(1'b0));
  Register #(.width(16)) R1 (.D(write_data), .en(and_2_out), .Q(R1_q), .clk(clock));  // open: clr
  Register #(.width(16)) R2 (.D(write_data), .en(and_3_out), .Q(R2_q), .clk(clock), .clr(1'b0));
  Register #(.width(16)) R3 (.D(write_data), .en(and_4_out), .Q(R3_q), .clk(clock), .clr(1'b0));
  Register #(.width(16)) R4 (.D(write_data), .en(and_5_out), .Q(R4_q), .clk(clock), .clr(1'b0));
  Register #(.width(16)) R5 (.D(write_data), .en(and_6_out), .Q(R5_q), .clk(clock), .clr(1'b0));
  Register #(.width(16)) R6 (.D(write_data), .en(and_7_out), .Q(R6_q), .clk(clock), .clr(1'b0));
  Register #(.width(16)) R7 (.D(write_data), .en(and_8_out), .Q(R7_q), .clk(clock), .clr(1'b0));
  Multiplexer #(.select(3), .width(16), .enable("false")) multiplexer_1 (
    .in0(R0_q), .in1(R1_q), .in2(R2_q), .in3(R3_q), .in4(R4_q), .in5(R5_q), .in6(R6_q), .in7(R7_q),
    .out(read_data_1), .sel(read_register_1));
  Multiplexer #(.select(3), .width(16), .enable("false")) multiplexer_2 (
    .in0(R0_q), .in1(R1_q), .in2(R2_q), .in3(R3_q), .in4(R4_q), .in5(R5_q), .in6(R6_q), .in7(R7_q),
    .out(read_data_2), .sel(read_register_2));
endmodule
